// Logisim project 16BitBinaryToGrey.circ as structural Verilog: 1 circuit, main circuit BIN_TO_GREY_16BIT
module BIN_TO_GREY_16BIT (
  input  B0,
  input  B1,
  input  B2,
  input  B3,
  input  B4,
  input  B5,
  input  B6,
  input  B7,
  input  B8,
  input  B9,
  input  B10,
  input  B11,
  input  B12,
  input  B13,
  input  B14,
  input  B15,
  output G0,
  output G1,
  output G2,
  output G3,
  output G4,
  output G5,
  output G6,
  output G7,
  output G8,
  output G9,
  output G10,
  output G11,
  output G12,
  output G13,
  output G14,
  output G15
);

  xor xor_1 (G14, B14, B15);
  xor xor_2 (G13, B13, B14);
  xor xor_3 (G12, B12, B13);
  xor xor_4 (G11, B11, B12);
  xor xor_5 (G10, B10, B11);
  xor xor_6 (G8, B8, B9);
  xor xor_7 (G9, B9, B10);
  xor xor_8 (G1, B1, B2);
  xor xor_9 (G2, B2, B3);
  xor xor_10 (G3, B3, B4);
  xor xor_11 (G4, B4, B5);
  xor xor_12 (G5, B5, B6);
  xor xor_13 (G6, B6, B7);
  xor xor_14 (G7, B7, B8);
  xor xor_15 (G0, B0, B1);

  assign G15 = B15;
endmodule
