// Logisim project 16BitGreyToBinary.circ as structural Verilog: 1 circuit, main circuit GREY_TO_BIN_16BIT
module GREY_TO_BIN_16BIT (
  input  G0,
  input  G1,
  input  G2,
  input  G3,
  input  G4,
  input  G5,
  input  G6,
  input  G7,
  input  G8,
  input  G9,
  input  G10,
  input  G11,
  input  G12,
  input  G13,
  input  G14,
  input  G15,
  output B0,
  output B1,
  output B2,
  output B3,
  output B4,
  output B5,
  output B6,
  output B7,
  output B8,
  output B9,
  output B10,
  output B11,
  output B12,
  output B13,
  output B14,
  output B15
);

  xor xor_1 (B14, G14, G15);
  xor xor_2 (B13, G13, B14);
  xor xor_3 (B12, G12, B13);
  xor xor_4 (B11, G11, B12);
  xor xor_5 (B10, G10, B11);
  xor xor_6 (B8, G8, B9);
  xor xor_7 (B9, G9, B10);
  xor xor_8 (B1, G1, B2);
  xor xor_9 (B2, G2, B3);
  xor xor_10 (B3, G3, B4);
  xor xor_11 (B4, G4, B5);
  xor xor_12 (B5, G5, B6);
  xor xor_13 (B6, G6, B7);
  xor xor_14 (B7, G7, B8);
  xor xor_15 (B0, G0, B1);

  assign B15 = G15;
endmodule
