// Logisim project 16BitMultiplier.circ as structural Verilog: 1 circuit, main circuit Multiplier_16_Bit
module Multiplier_16_Bit (
  input  B15,
  input  B14,
  input  B13,
  input  B12,
  input  B11,
  input  B10,
  input  B9,
  input  B8,
  input  B7,
  input  B6,
  input  B5,
  input  B4,
  input  B3,
  input  B2,
  input  B1,
  input  B0,
  input  A15,
  input  A14,
  input  A13,
  input  A12,
  input  A11,
  input  A10,
  input  A9,
  input  A8,
  input  A7,
  input  A6,
  input  A5,
  input  A4,
  input  A3,
  input  A2,
  input  A1,
  input  A0,
  output P31,
  output P30,
  output P29,
  output P28,
  output P27,
  output P26,
  output P25,
  output P24,
  output P23,
  output P22,
  output P21,
  output P20,
  output P19,
  output P18,
  output P17,
  output P16,
  output P15,
  output P14,
  output P13,
  output P12,
  output P11,
  output P10,
  output P9,
  output P8,
  output P7,
  output P6,
  output P5,
  output P4,
  output P3,
  output P2,
  output P1,
  output P0
);

  wire [14:0] and_255_out;
  wire [15:0] adder_2_cout, adder_3_cout, adder_4_cout, adder_5_cout, adder_6_cout, adder_7_cout,
       adder_8_cout, adder_9_cout, adder_10_cout, adder_13_cout, adder_14_cout, adder_15_cout, and_16_out,
       and_32_out, and_48_out, and_64_out, and_80_out, and_96_out, and_112_out, and_128_out, and_144_out,
       and_160_out, and_176_out, and_192_out, and_208_out, and_224_out, and_240_out;
  wire [15:1] adder_11_out, adder_12_out;
  wire [15:15] adder_11_cout, adder_12_cout;

  and and_1 (and_16_out[15], A15, B15);
  and and_2 (and_16_out[14], A15, B14);
  and and_3 (and_16_out[13], A15, B13);
  and and_4 (and_16_out[12], A15, B12);
  and and_5 (and_16_out[11], A15, B11);
  and and_6 (and_16_out[10], A15, B10);
  and and_7 (and_16_out[9], A15, B9);
  and and_8 (and_16_out[8], A15, B8);
  and and_9 (and_16_out[7], A15, B7);
  and and_10 (and_16_out[6], A15, B6);
  and and_11 (and_16_out[5], A15, B5);
  and and_12 (and_16_out[4], A15, B4);
  and and_13 (and_16_out[3], A15, B3);
  and and_14 (and_16_out[2], A15, B2);
  and and_15 (and_16_out[1], A15, B1);
  and and_16 (and_16_out[0], A15, B0);
  and and_17 (and_32_out[15], A14, B15);
  and and_18 (and_32_out[14], A14, B14);
  and and_19 (and_32_out[13], A14, B13);
  and and_20 (and_32_out[12], A14, B12);
  and and_21 (and_32_out[11], A14, B11);
  and and_22 (and_32_out[10], A14, B10);
  and and_23 (and_32_out[9], A14, B9);
  and and_24 (and_32_out[8], A14, B8);
  and and_25 (and_32_out[7], A14, B7);
  and and_26 (and_32_out[6], A14, B6);
  Adder #(.width(16)) adder_1 (
    .a(adder_2_cout), .b(and_16_out),
    .out({P30, P29, P28, P27, P26, P25, P24, P23, P22, P21, P20, P19, P18, P17, P16, P15}), .cin(1'b0),
    .cout(P31));
  and and_27 (and_32_out[5], A14, B5);
  and and_28 (and_32_out[4], A14, B4);
  and and_29 (and_32_out[3], A14, B3);
  and and_30 (and_32_out[2], A14, B2);
  and and_31 (and_32_out[1], A14, B1);
  and and_32 (and_32_out[0], A14, B0);
  and and_33 (and_48_out[15], A13, B15);
  and and_34 (and_48_out[14], A13, B14);
  and and_35 (and_48_out[13], A13, B13);
  and and_36 (and_48_out[12], A13, B12);
  and and_37 (and_48_out[11], A13, B11);
  and and_38 (and_48_out[10], A13, B10);
  and and_39 (and_48_out[9], A13, B9);
  and and_40 (and_48_out[8], A13, B8);
  Adder #(.width(16)) adder_2 (
    .a(adder_3_cout), .b(and_32_out), .out({adder_2_cout[14:0], P14}), .cin(1'b0), .cout(adder_2_cout[15]));
  and and_41 (and_48_out[7], A13, B7);
  and and_42 (and_48_out[6], A13, B6);
  and and_43 (and_48_out[5], A13, B5);
  and and_44 (and_48_out[4], A13, B4);
  and and_45 (and_48_out[3], A13, B3);
  and and_46 (and_48_out[2], A13, B2);
  and and_47 (and_48_out[1], A13, B1);
  and and_48 (and_48_out[0], A13, B0);
  and and_49 (and_64_out[15], A12, B15);
  and and_50 (and_64_out[14], A12, B14);
  and and_51 (and_64_out[13], A12, B13);
  and and_52 (and_64_out[12], A12, B12);
  and and_53 (and_64_out[11], A12, B11);
  and and_54 (and_64_out[10], A12, B10);
  and and_55 (and_64_out[9], A12, B9);
  Adder #(.width(16)) adder_3 (
    .a(adder_4_cout), .b(and_48_out), .out({adder_3_cout[14:0], P13}), .cin(1'b0), .cout(adder_3_cout[15]));
  and and_56 (and_64_out[8], A12, B8);
  and and_57 (and_64_out[7], A12, B7);
  and and_58 (and_64_out[6], A12, B6);
  and and_59 (and_64_out[5], A12, B5);
  and and_60 (and_64_out[4], A12, B4);
  and and_61 (and_64_out[3], A12, B3);
  and and_62 (and_64_out[2], A12, B2);
  and and_63 (and_64_out[1], A12, B1);
  and and_64 (and_64_out[0], A12, B0);
  and and_65 (and_80_out[15], A11, B15);
  and and_66 (and_80_out[14], A11, B14);
  and and_67 (and_80_out[13], A11, B13);
  and and_68 (and_80_out[12], A11, B12);
  and and_69 (and_80_out[11], A11, B11);
  Adder #(.width(16)) adder_4 (
    .a(adder_5_cout), .b(and_64_out), .out({adder_4_cout[14:0], P12}), .cin(1'b0), .cout(adder_4_cout[15]));
  and and_70 (and_80_out[10], A11, B10);
  and and_71 (and_80_out[9], A11, B9);
  and and_72 (and_80_out[8], A11, B8);
  and and_73 (and_80_out[7], A11, B7);
  and and_74 (and_80_out[6], A11, B6);
  and and_75 (and_80_out[5], A11, B5);
  and and_76 (and_80_out[4], A11, B4);
  and and_77 (and_80_out[3], A11, B3);
  and and_78 (and_80_out[2], A11, B2);
  and and_79 (and_80_out[1], A11, B1);
  and and_80 (and_80_out[0], A11, B0);
  and and_81 (and_96_out[15], A10, B15);
  and and_82 (and_96_out[14], A10, B14);
  and and_83 (and_96_out[13], A10, B13);
  Adder #(.width(16)) adder_5 (
    .a(adder_6_cout), .b(and_80_out), .out({adder_5_cout[14:0], P11}), .cin(1'b0), .cout(adder_5_cout[15]));
  and and_84 (and_96_out[12], A10, B12);
  and and_85 (and_96_out[11], A10, B11);
  and and_86 (and_96_out[10], A10, B10);
  and and_87 (and_96_out[9], A10, B9);
  and and_88 (and_96_out[8], A10, B8);
  and and_89 (and_96_out[7], A10, B7);
  and and_90 (and_96_out[6], A10, B6);
  and and_91 (and_96_out[5], A10, B5);
  and and_92 (and_96_out[4], A10, B4);
  and and_93 (and_96_out[3], A10, B3);
  and and_94 (and_96_out[2], A10, B2);
  and and_95 (and_96_out[1], A10, B1);
  and and_96 (and_96_out[0], A10, B0);
  and and_97 (and_112_out[15], A9, B15);
  Adder #(.width(16)) adder_6 (
    .a(adder_7_cout), .b(and_96_out), .out({adder_6_cout[14:0], P10}), .cin(1'b0), .cout(adder_6_cout[15]));
  and and_98 (and_112_out[14], A9, B14);
  and and_99 (and_112_out[13], A9, B13);
  and and_100 (and_112_out[12], A9, B12);
  and and_101 (and_112_out[11], A9, B11);
  and and_102 (and_112_out[10], A9, B10);
  and and_103 (and_112_out[9], A9, B9);
  and and_104 (and_112_out[8], A9, B8);
  and and_105 (and_112_out[7], A9, B7);
  and and_106 (and_112_out[6], A9, B6);
  and and_107 (and_112_out[5], A9, B5);
  and and_108 (and_112_out[4], A9, B4);
  and and_109 (and_112_out[3], A9, B3);
  and and_110 (and_112_out[2], A9, B2);
  and and_111 (and_112_out[1], A9, B1);
  and and_112 (and_112_out[0], A9, B0);
  and and_113 (and_128_out[15], A8, B15);
  and and_114 (and_128_out[14], A8, B14);
  and and_115 (and_128_out[13], A8, B13);
  Adder #(.width(16)) adder_7 (
    .a(adder_8_cout), .b(and_112_out), .out({adder_7_cout[14:0], P9}), .cin(1'b0), .cout(adder_7_cout[15]));
  and and_116 (and_128_out[12], A8, B12);
  and and_117 (and_128_out[11], A8, B11);
  and and_118 (and_128_out[10], A8, B10);
  and and_119 (and_128_out[9], A8, B9);
  and and_120 (and_128_out[8], A8, B8);
  and and_121 (and_128_out[7], A8, B7);
  and and_122 (and_128_out[6], A8, B6);
  and and_123 (and_128_out[5], A8, B5);
  and and_124 (and_128_out[4], A8, B4);
  and and_125 (and_128_out[3], A8, B3);
  and and_126 (and_128_out[2], A8, B2);
  and and_127 (and_128_out[1], A8, B1);
  and and_128 (and_128_out[0], A8, B0);
  and and_129 (and_144_out[15], A7, B15);
  Adder #(.width(16)) adder_8 (
    .a(adder_9_cout), .b(and_128_out), .out({adder_8_cout[14:0], P8}), .cin(1'b0), .cout(adder_8_cout[15]));
  and and_130 (and_144_out[14], A7, B14);
  and and_131 (and_144_out[13], A7, B13);
  and and_132 (and_144_out[12], A7, B12);
  and and_133 (and_144_out[11], A7, B11);
  and and_134 (and_144_out[10], A7, B10);
  and and_135 (and_144_out[9], A7, B9);
  and and_136 (and_144_out[8], A7, B8);
  and and_137 (and_144_out[7], A7, B7);
  and and_138 (and_144_out[6], A7, B6);
  and and_139 (and_144_out[5], A7, B5);
  and and_140 (and_144_out[4], A7, B4);
  and and_141 (and_144_out[3], A7, B3);
  and and_142 (and_144_out[2], A7, B2);
  and and_143 (and_144_out[1], A7, B1);
  and and_144 (and_144_out[0], A7, B0);
  and and_145 (and_160_out[15], A6, B15);
  Adder #(.width(16)) adder_9 (
    .a(adder_10_cout), .b(and_144_out), .out({adder_9_cout[14:0], P7}), .cin(1'b0), .cout(adder_9_cout[15]));
  and and_146 (and_160_out[14], A6, B14);
  and and_147 (and_160_out[13], A6, B13);
  and and_148 (and_160_out[12], A6, B12);
  and and_149 (and_160_out[11], A6, B11);
  and and_150 (and_160_out[10], A6, B10);
  and and_151 (and_160_out[9], A6, B9);
  and and_152 (and_160_out[8], A6, B8);
  and and_153 (and_160_out[7], A6, B7);
  and and_154 (and_160_out[6], A6, B6);
  and and_155 (and_160_out[5], A6, B5);
  and and_156 (and_160_out[4], A6, B4);
  and and_157 (and_160_out[3], A6, B3);
  and and_158 (and_160_out[2], A6, B2);
  and and_159 (and_160_out[1], A6, B1);
  and and_160 (and_160_out[0], A6, B0);
  Adder #(.width(16)) adder_10 (
    .a({adder_11_cout[15], adder_11_out}), .b(and_160_out), .out({adder_10_cout[14:0], P6}), .cin(1'b0),
    .cout(adder_10_cout[15]));
  and and_161 (and_176_out[15], A5, B15);
  and and_162 (and_176_out[14], A5, B14);
  and and_163 (and_176_out[13], A5, B13);
  and and_164 (and_176_out[12], A5, B12);
  and and_165 (and_176_out[11], A5, B11);
  and and_166 (and_176_out[10], A5, B10);
  and and_167 (and_176_out[9], A5, B9);
  and and_168 (and_176_out[8], A5, B8);
  and and_169 (and_176_out[7], A5, B7);
  and and_170 (and_176_out[6], A5, B6);
  and and_171 (and_176_out[5], A5, B5);
  and and_172 (and_176_out[4], A5, B4);
  and and_173 (and_176_out[3], A5, B3);
  and and_174 (and_176_out[2], A5, B2);
  and and_175 (and_176_out[1], A5, B1);
  and and_176 (and_176_out[0], A5, B0);
  Adder #(.width(16)) adder_11 (
    .a({adder_12_cout[15], adder_12_out}), .b(and_176_out), .out({adder_11_out, P5}), .cin(1'b0),
    .cout(adder_11_cout[15]));
  and and_177 (and_192_out[15], A4, B15);
  and and_178 (and_192_out[14], A4, B14);
  and and_179 (and_192_out[13], A4, B13);
  and and_180 (and_192_out[12], A4, B12);
  and and_181 (and_192_out[11], A4, B11);
  and and_182 (and_192_out[10], A4, B10);
  and and_183 (and_192_out[9], A4, B9);
  and and_184 (and_192_out[8], A4, B8);
  and and_185 (and_192_out[7], A4, B7);
  and and_186 (and_192_out[6], A4, B6);
  and and_187 (and_192_out[5], A4, B5);
  and and_188 (and_192_out[4], A4, B4);
  and and_189 (and_192_out[3], A4, B3);
  and and_190 (and_192_out[2], A4, B2);
  and and_191 (and_192_out[1], A4, B1);
  and and_192 (and_192_out[0], A4, B0);
  Adder #(.width(16)) adder_12 (
    .a(adder_13_cout), .b(and_192_out), .out({adder_12_out, P4}), .cin(1'b0), .cout(adder_12_cout[15]));
  and and_193 (and_208_out[15], A3, B15);
  and and_194 (and_208_out[14], A3, B14);
  and and_195 (and_208_out[13], A3, B13);
  and and_196 (and_208_out[12], A3, B12);
  and and_197 (and_208_out[11], A3, B11);
  and and_198 (and_208_out[10], A3, B10);
  and and_199 (and_208_out[9], A3, B9);
  and and_200 (and_208_out[8], A3, B8);
  and and_201 (and_208_out[7], A3, B7);
  and and_202 (and_208_out[6], A3, B6);
  and and_203 (and_208_out[5], A3, B5);
  and and_204 (and_208_out[4], A3, B4);
  and and_205 (and_208_out[3], A3, B3);
  and and_206 (and_208_out[2], A3, B2);
  and and_207 (and_208_out[1], A3, B1);
  and and_208 (and_208_out[0], A3, B0);
  Adder #(.width(16)) adder_13 (
    .a(adder_14_cout), .b(and_208_out), .out({adder_13_cout[14:0], P3}), .cin(1'b0), .cout(adder_13_cout[15]));
  and and_209 (and_224_out[15], A2, B15);
  and and_210 (and_224_out[14], A2, B14);
  and and_211 (and_224_out[13], A2, B13);
  and and_212 (and_224_out[12], A2, B12);
  and and_213 (and_224_out[11], A2, B11);
  and and_214 (and_224_out[10], A2, B10);
  and and_215 (and_224_out[9], A2, B9);
  and and_216 (and_224_out[8], A2, B8);
  and and_217 (and_224_out[7], A2, B7);
  and and_218 (and_224_out[6], A2, B6);
  and and_219 (and_224_out[5], A2, B5);
  and and_220 (and_224_out[4], A2, B4);
  and and_221 (and_224_out[3], A2, B3);
  and and_222 (and_224_out[2], A2, B2);
  and and_223 (and_224_out[1], A2, B1);
  and and_224 (and_224_out[0], A2, B0);
  Adder #(.width(16)) adder_14 (
    .a(adder_15_cout), .b(and_224_out), .out({adder_14_cout[14:0], P2}), .cin(1'b0), .cout(adder_14_cout[15]));
  and and_225 (and_240_out[15], A1, B15);
  and and_226 (and_240_out[14], A1, B14);
  and and_227 (and_240_out[13], A1, B13);
  and and_228 (and_240_out[12], A1, B12);
  and and_229 (and_240_out[11], A1, B11);
  and and_230 (and_240_out[10], A1, B10);
  and and_231 (and_240_out[9], A1, B9);
  and and_232 (and_240_out[8], A1, B8);
  and and_233 (and_240_out[7], A1, B7);
  and and_234 (and_240_out[6], A1, B6);
  and and_235 (and_240_out[5], A1, B5);
  and and_236 (and_240_out[4], A1, B4);
  and and_237 (and_240_out[3], A1, B3);
  and and_238 (and_240_out[2], A1, B2);
  and and_239 (and_240_out[1], A1, B1);
  and and_240 (and_240_out[0], A1, B0);
  and and_241 (and_255_out[14], A0, B15);
  and and_242 (and_255_out[13], A0, B14);
  Adder #(.width(16)) adder_15 (
    .a({1'b0, and_255_out}), .b(and_240_out), .out({adder_15_cout[14:0], P1}), .cin(1'b0),
    .cout(adder_15_cout[15]));
  and and_243 (and_255_out[12], A0, B13);
  and and_244 (and_255_out[11], A0, B12);
  and and_245 (and_255_out[10], A0, B11);
  and and_246 (and_255_out[9], A0, B10);
  and and_247 (and_255_out[8], A0, B9);
  and and_248 (and_255_out[7], A0, B8);
  and and_249 (and_255_out[6], A0, B7);
  and and_250 (and_255_out[5], A0, B6);
  and and_251 (and_255_out[4], A0, B5);
  and and_252 (and_255_out[3], A0, B4);
  and and_253 (and_255_out[2], A0, B3);
  and and_254 (and_255_out[1], A0, B2);
  and and_255 (and_255_out[0], A0, B1);
  and and_256 (P0, A0, B0);
endmodule
