// Logisim project 16BitNOT.circ as structural Verilog: 1 circuit, main circuit NOT_16BIT
module NOT_16BIT (
  input  A0,
  input  A1,
  input  A2,
  input  A3,
  input  A4,
  input  A5,
  input  A6,
  input  A7,
  input  A8,
  input  A9,
  input  A10,
  input  A11,
  input  A12,
  input  A13,
  input  A14,
  input  A15,
  output X0,
  output X1,
  output X2,
  output X3,
  output X4,
  output X5,
  output X6,
  output X7,
  output X8,
  output X9,
  output X10,
  output X11,
  output X12,
  output X13,
  output X14,
  output X15
);

  not not_1 (X0, A0);
  not not_2 (X1, A1);
  not not_3 (X2, A2);
  not not_4 (X3, A3);
  not not_5 (X4, A4);
  not not_6 (X5, A5);
  not not_7 (X6, A6);
  not not_8 (X7, A7);
  not not_9 (X8, A8);
  not not_10 (X9, A9);
  not not_11 (X10, A10);
  not not_12 (X11, A11);
  not not_13 (X12, A12);
  not not_14 (X13, A13);
  not not_15 (X14, A14);
  not not_16 (X15, A15);
endmodule
