// Logisim project 16BitXOR.circ as structural Verilog: 1 circuit, main circuit XOR_16BIT
module XOR_16BIT (
  input  A0,
  input  A1,
  input  A2,
  input  A3,
  input  A4,
  input  A5,
  input  A6,
  input  A7,
  input  A8,
  input  A9,
  input  A10,
  input  A11,
  input  A12,
  input  A13,
  input  A14,
  input  A15,
  input  B0,
  input  B1,
  input  B2,
  input  B3,
  input  B4,
  input  B5,
  input  B6,
  input  B7,
  input  B8,
  input  B9,
  input  B10,
  input  B11,
  input  B12,
  input  B13,
  input  B14,
  input  B15,
  output X0,
  output X1,
  output X2,
  output X3,
  output X4,
  output X5,
  output X6,
  output X7,
  output X8,
  output X9,
  output X10,
  output X11,
  output X12,
  output X13,
  output X14,
  output X15
);

  xor xor_1 (X0, A0, B0);
  xor xor_2 (X1, A1, B1);
  xor xor_3 (X2, A2, B2);
  xor xor_4 (X3, A3, B3);
  xor xor_5 (X4, A4, B4);
  xor xor_6 (X5, A5, B5);
  xor xor_7 (X6, A6, B6);
  xor xor_8 (X7, A7, B7);
  xor xor_9 (X8, A8, B8);
  xor xor_10 (X9, A9, B9);
  xor xor_11 (X10, A10, B10);
  xor xor_12 (X11, A11, B11);
  xor xor_13 (X12, A12, B12);
  xor xor_14 (X13, A13, B13);
  xor xor_15 (X14, A14, B14);
  xor xor_16 (X15, A15, B15);
endmodule
