// Logisim project 16Bit_BitwiseRightShift.circ as structural Verilog: 1 circuit, main circuit Bitwise_Right_Shift
module Bitwise_Right_Shift (
  input  A0,
  input  A1,
  input  A2,
  input  A3,
  input  A4,
  input  A5,
  input  A6,
  input  A7,
  input  A8,
  input  A9,
  input  A10,
  input  A11,
  input  A12,
  input  A13,
  input  A14,
  input  A15,
  output X0,
  output X1,
  output X2,
  output X3,
  output X4,
  output X5,
  output X6,
  output X7,
  output X8,
  output X9,
  output X10,
  output X11,
  output X12,
  output X13,
  output X14,
  output X15
);


  assign X0 = A1;
  assign X1 = A2;
  assign X2 = A3;
  assign X3 = A4;
  assign X4 = A5;
  assign X5 = A6;
  assign X6 = A7;
  assign X7 = A8;
  assign X8 = A9;
  assign X9 = A10;
  assign X10 = A11;
  assign X11 = A12;
  assign X12 = A13;
  assign X13 = A14;
  assign X14 = A15;
  assign X15 = 1'b0;
endmodule
