// Logisim project 16Bit_Log2.circ as structural Verilog: 1 circuit, main circuit Log2
module Log2 (
  input  A0,
  input  A1,
  input  A2,
  input  A3,
  input  A4,
  input  A5,
  input  A6,
  input  A7,
  input  A8,
  input  A9,
  input  A10,
  input  A11,
  input  A12,
  input  A13,
  input  A14,
  input  A15,
  output [1:0] Undefined_Value,
  output B0,
  output B1,
  output B2,
  output B3
);

  Priority_Encoder #(.select(4)) priority_encoder_1 (
    .in0(A0), .in1(A1), .in2(A2), .in3(A3), .in4(A4), .in5(A5), .in6(A6), .in7(A7), .in8(A8), .in9(A9),
    .in10(A10), .in11(A11), .in12(A12), .in13(A13), .in14(A14), .in15(A15), .out({B3, B2, B1, B0}),
    .en_out(Undefined_Value[1]), .en_in(1'b1));  // open: gs
  not not_1 (Undefined_Value[0], Undefined_Value[1]);
endmodule
