// Logisim project Divisor_Block.circ as structural Verilog: 1 circuit, main circuit Divisor_Block
module Divisor_Block (
  input  Cin,
  input  A,
  input  B,
  input  Selection,
  output OUTPUTT,
  output Cout
);

  wire adder_1_out, not_1_out;

  not not_1 (not_1_out, B);
  Adder #(.width(1)) adder_1 (.a(A), .b(not_1_out), .out(adder_1_out), .cin(Cin), .cout(Cout));
  Multiplexer multiplexer_1 (.in0(A), .in1(adder_1_out), .out(OUTPUTT), .sel(Selection));
endmodule
