// Logisim project Divisor_Converter.circ as structural Verilog: 1 circuit, main circuit Converter
module Converter (
  input  [31:0] Inputt,
  output [15:0] Decimal_Quotient,
  output [15:0] Binary_Quotient,
  output [7:0] Decimal_Remainder,
  output [7:0] Binary_Remainder
);


  assign Binary_Quotient = Inputt[15:0];
  assign Binary_Remainder = {Inputt[24], Inputt[25], Inputt[26], Inputt[27], Inputt[28], Inputt[29], Inputt[30], Inputt[31]};
  assign Decimal_Quotient = Inputt[15:0];
  assign Decimal_Remainder = {Inputt[24], Inputt[25], Inputt[26], Inputt[27], Inputt[28], Inputt[29], Inputt[30], Inputt[31]};
endmodule
