// Logisim project FINAL.circ as structural Verilog: 1 circuit, main circuit main
module main (
  input  in_1,
  input  in_2,
  input  in_3,
  input  in_4,
  input  in_5,
  input  in_6,
  input  in_7,
  input  in_8,
  input  in_9,
  input  in_10,
  input  in_11,
  input  in_12,
  input  in_13,
  input  in_14,
  input  in_15,
  input  in_16,
  input  in_17,
  input  in_18,
  input  in_19,
  input  in_20,
  input  in_21,
  input  in_22,
  input  in_23,
  input  in_24,
  input  in_25,
  input  in_26,
  input  in_27,
  input  in_28,
  input  in_29,
  input  in_30,
  input  in_31,
  input  in_32,
  input  in_33,
  input  in_34,
  input  in_35,
  input  in_36,
  input  in_37,
  input  in_38,
  input  in_39,
  input  in_40,
  input  in_41,
  input  in_42,
  input  in_43,
  input  in_44,
  input  in_45,
  input  in_46,
  input  in_47,
  input  in_48,
  input  in_49,
  input  in_50,
  input  in_51,
  input  in_52,
  input  in_53,
  input  in_54,
  input  in_55,
  input  in_56,
  input  in_57,
  input  in_58,
  input  in_59,
  input  in_60,
  input  in_61,
  input  in_62,
  input  in_63,
  input  in_64,
  input  in_65,
  input  in_66,
  input  in_67,
  input  in_68,
  input  in_69,
  input  in_70,
  input  in_71,
  input  in_72,
  input  in_73,
  input  in_74,
  input  in_75,
  input  in_76,
  input  in_77,
  input  in_78,
  input  in_79,
  input  in_80,
  input  in_81,
  input  in_82,
  input  in_83,
  input  B15,
  input  in_85,
  input  B14,
  input  in_87,
  input  B13,
  input  in_89,
  input  B12,
  input  in_91,
  input  B11,
  input  in_93,
  input  B10,
  input  in_95,
  input  B9,
  input  in_97,
  input  B8,
  input  in_99,
  input  B7,
  input  in_101,
  input  B6,
  input  in_103,
  input  B5,
  input  in_105,
  input  B4,
  input  B3,
  input  B2,
  input  B1,
  input  B0,
  input  A15,
  input  A14,
  input  A13,
  input  A12,
  input  A11,
  input  A10,
  input  A9,
  input  A8,
  input  A7,
  input  A6,
  input  A5,
  input  A4,
  input  A3,
  input  A2,
  input  in_125,
  input  A1,
  input  A0,
  input  in_128,
  input  in_129,
  input  in_130,
  input  in_131,
  input  in_132,
  input  in_133,
  input  in_134,
  input  in_135,
  input  in_136,
  input  in_137,
  input  in_138,
  input  in_139,
  input  in_140,
  input  in_141,
  input  in_142,
  input  in_143,
  input  in_144,
  input  in_145,
  input  in_146,
  input  in_147,
  input  in_148,
  input  in_149,
  input  in_150,
  input  in_151,
  input  in_152,
  input  in_153,
  input  in_154,
  input  in_155,
  input  in_156,
  input  in_157,
  input  in_158,
  input  in_159,
  input  in_160,
  input  in_161,
  input  in_162,
  input  in_163,
  input  in_164,
  input  in_165,
  input  in_166,
  input  in_167,
  input  in_168,
  input  in_169,
  input  in_170,
  input  in_171,
  input  in_172,
  input  in_173,
  input  in_174,
  input  in_175,
  input  in_176,
  input  in_177,
  input  in_178,
  input  in_179,
  input  in_180,
  input  in_181,
  input  in_182,
  input  in_183,
  input  in_184,
  input  in_185,
  input  in_186,
  input  in_187,
  input  in_188,
  input  in_189,
  input  in_190,
  input  in_191,
  input  in_192,
  input  in_193,
  input  in_194,
  input  in_195,
  input  in_196,
  input  in_197,
  input  in_198,
  input  in_199,
  input  in_200,
  input  in_201,
  input  in_202,
  input  in_203,
  input  in_204,
  input  in_205,
  input  in_206,
  input  [3:0] in_207,
  input  in_208,
  input  RESET,
  input  A,
  input  B,
  input  C,
  input  D,
  input  [7:0] Divisor_Decimal,
  input  [7:0] Divisor_Binary,
  input  in_216,
  input  [15:0] Dividend_Decimal,
  input  [15:0] Dividend_Binary,
  input  RESETT,
  input  [15:0] DECIMEL_POWER_INPUT,
  input  [15:0] BINARY_POWER_INPUT,
  input  in_222,
  input  [7:0] DECIMAL_POWER,
  input  [7:0] BINARY_POWER,
  output [15:0] Decimal_Quotient,
  output [15:0] Binary_Quotient,
  output [7:0] Decimal_Remainder,
  output [7:0] Binay_Remainder,
  output [31:0] Decimal,
  output [31:0] Binary
);

  wire clock_1_out, clock_2_out;
  wire [1:0] divisor_16bit_1_undefined, factorial_0to9_1_overflow, log2_1_undefined_value;
  wire [3:0] log2_1_b0;
  wire [7:0] multiplexer_3_out, multiplexer_4_out;
  wire [15:0] and_16bit_1_x0, bin_to_grey_16bit_1_g0, bitwise_left_shift_1_x0, bitwise_right_shift_1_x0,
       divisor_16bit_1_q0, grey_to_bin_16bit_1_b0, multiplexer_1_out, multiplexer_2_out, multiplexer_5_out,
       not_16bit_1_x0, or_16bit_1_x0, subractor_16_bit_1_s0, xnor_16bit_1_x0, xor_16bit_1_x0;
  wire [16:0] adder_16_bit_1_s0;
  wire [31:0] factorial_0to9_1_answer, mul_16_bit_1_p0, power_16bit_1_outputtt;
  wire [31:24] divisor_16bit_1_r7;

  Multiplexer #(.width(16)) multiplexer_1 (
    .in0({B15, B14, B13, B12, B11, B10, B9, B8, B7, B6, B5, B4, B3, B2, B1, B0}),
    .in1({A15, A14, A13, A12, A11, A10, A9, A8, A7, A6, A5, A4, A3, A2, A1, A0}), .out(multiplexer_1_out),
    .sel(in_125));
  Clock clock_1 (.out(clock_1_out));
  Clock clock_2 (.out(clock_2_out));
  Multiplexer #(.width(16)) multiplexer_2 (
    .in0(DECIMEL_POWER_INPUT), .in1(BINARY_POWER_INPUT), .out(multiplexer_2_out), .sel(in_222));
  Multiplexer #(.width(8)) multiplexer_3 (
    .in0(DECIMAL_POWER), .in1(BINARY_POWER), .out(multiplexer_3_out), .sel(in_222));
  Multiplexer #(.width(8)) multiplexer_4 (
    .in0(Divisor_Decimal), .in1(Divisor_Binary), .out(multiplexer_4_out), .sel(in_216));
  Multiplexer #(.width(16)) multiplexer_5 (
    .in0(Dividend_Decimal), .in1(Dividend_Binary), .out(multiplexer_5_out), .sel(in_216));
  BIN_TO_GREY_16BIT bin_to_grey_16bit_1 (
    .B0(multiplexer_1_out[0]), .B1(multiplexer_1_out[1]), .B2(multiplexer_1_out[2]),
    .B3(multiplexer_1_out[3]), .B4(multiplexer_1_out[4]), .B5(multiplexer_1_out[5]),
    .B6(multiplexer_1_out[6]), .B7(multiplexer_1_out[7]), .B8(multiplexer_1_out[8]),
    .B9(multiplexer_1_out[9]), .B10(multiplexer_1_out[10]), .B11(multiplexer_1_out[11]),
    .B12(multiplexer_1_out[12]), .B13(multiplexer_1_out[13]), .B14(multiplexer_1_out[14]),
    .B15(multiplexer_1_out[15]), .G0(bin_to_grey_16bit_1_g0[0]), .G1(bin_to_grey_16bit_1_g0[1]),
    .G2(bin_to_grey_16bit_1_g0[2]), .G3(bin_to_grey_16bit_1_g0[3]), .G4(bin_to_grey_16bit_1_g0[4]),
    .G5(bin_to_grey_16bit_1_g0[5]), .G6(bin_to_grey_16bit_1_g0[6]), .G7(bin_to_grey_16bit_1_g0[7]),
    .G8(bin_to_grey_16bit_1_g0[8]), .G9(bin_to_grey_16bit_1_g0[9]), .G10(bin_to_grey_16bit_1_g0[10]),
    .G11(bin_to_grey_16bit_1_g0[11]), .G12(bin_to_grey_16bit_1_g0[12]), .G13(bin_to_grey_16bit_1_g0[13]),
    .G14(bin_to_grey_16bit_1_g0[14]), .G15(bin_to_grey_16bit_1_g0[15]));
  Bitwise_Left_Shift bitwise_left_shift_1 (
    .A0(multiplexer_1_out[0]), .A1(multiplexer_1_out[1]), .A2(multiplexer_1_out[2]),
    .A3(multiplexer_1_out[3]), .A4(multiplexer_1_out[4]), .A5(multiplexer_1_out[5]),
    .A6(multiplexer_1_out[6]), .A7(multiplexer_1_out[7]), .A8(multiplexer_1_out[8]),
    .A9(multiplexer_1_out[9]), .A10(multiplexer_1_out[10]), .A11(multiplexer_1_out[11]),
    .A12(multiplexer_1_out[12]), .A13(multiplexer_1_out[13]), .A14(multiplexer_1_out[14]),
    .A15(multiplexer_1_out[15]), .X0(bitwise_left_shift_1_x0[0]), .X1(bitwise_left_shift_1_x0[1]),
    .X2(bitwise_left_shift_1_x0[2]), .X3(bitwise_left_shift_1_x0[3]), .X4(bitwise_left_shift_1_x0[4]),
    .X5(bitwise_left_shift_1_x0[5]), .X6(bitwise_left_shift_1_x0[6]), .X7(bitwise_left_shift_1_x0[7]),
    .X8(bitwise_left_shift_1_x0[8]), .X9(bitwise_left_shift_1_x0[9]), .X10(bitwise_left_shift_1_x0[10]),
    .X11(bitwise_left_shift_1_x0[11]), .X12(bitwise_left_shift_1_x0[12]), .X13(bitwise_left_shift_1_x0[13]),
    .X14(bitwise_left_shift_1_x0[14]), .X15(bitwise_left_shift_1_x0[15]));
  Bitwise_Right_Shift bitwise_right_shift_1 (
    .A0(multiplexer_1_out[0]), .A1(multiplexer_1_out[1]), .A2(multiplexer_1_out[2]),
    .A3(multiplexer_1_out[3]), .A4(multiplexer_1_out[4]), .A5(multiplexer_1_out[5]),
    .A6(multiplexer_1_out[6]), .A7(multiplexer_1_out[7]), .A8(multiplexer_1_out[8]),
    .A9(multiplexer_1_out[9]), .A10(multiplexer_1_out[10]), .A11(multiplexer_1_out[11]),
    .A12(multiplexer_1_out[12]), .A13(multiplexer_1_out[13]), .A14(multiplexer_1_out[14]),
    .A15(multiplexer_1_out[15]), .X0(bitwise_right_shift_1_x0[0]), .X1(bitwise_right_shift_1_x0[1]),
    .X2(bitwise_right_shift_1_x0[2]), .X3(bitwise_right_shift_1_x0[3]), .X4(bitwise_right_shift_1_x0[4]),
    .X5(bitwise_right_shift_1_x0[5]), .X6(bitwise_right_shift_1_x0[6]), .X7(bitwise_right_shift_1_x0[7]),
    .X8(bitwise_right_shift_1_x0[8]), .X9(bitwise_right_shift_1_x0[9]), .X10(bitwise_right_shift_1_x0[10]),
    .X11(bitwise_right_shift_1_x0[11]), .X12(bitwise_right_shift_1_x0[12]),
    .X13(bitwise_right_shift_1_x0[13]), .X14(bitwise_right_shift_1_x0[14]), .X15(bitwise_right_shift_1_x0[15]));
  NOT_16BIT not_16bit_1 (
    .A0(multiplexer_1_out[0]), .A1(multiplexer_1_out[1]), .A2(multiplexer_1_out[2]),
    .A3(multiplexer_1_out[3]), .A4(multiplexer_1_out[4]), .A5(multiplexer_1_out[5]),
    .A6(multiplexer_1_out[6]), .A7(multiplexer_1_out[7]), .A8(multiplexer_1_out[8]),
    .A9(multiplexer_1_out[9]), .A10(multiplexer_1_out[10]), .A11(multiplexer_1_out[11]),
    .A12(multiplexer_1_out[12]), .A13(multiplexer_1_out[13]), .A14(multiplexer_1_out[14]),
    .A15(multiplexer_1_out[15]), .X0(not_16bit_1_x0[0]), .X1(not_16bit_1_x0[1]), .X2(not_16bit_1_x0[2]),
    .X3(not_16bit_1_x0[3]), .X4(not_16bit_1_x0[4]), .X5(not_16bit_1_x0[5]), .X6(not_16bit_1_x0[6]),
    .X7(not_16bit_1_x0[7]), .X8(not_16bit_1_x0[8]), .X9(not_16bit_1_x0[9]), .X10(not_16bit_1_x0[10]),
    .X11(not_16bit_1_x0[11]), .X12(not_16bit_1_x0[12]), .X13(not_16bit_1_x0[13]), .X14(not_16bit_1_x0[14]),
    .X15(not_16bit_1_x0[15]));
  Factorial_0to9 factorial_0to9_1 (
    .RESET(RESET), .CLK(clock_1_out), .A0(A), .A1(B), .A2(C), .A3(D), .OVERFLOW(factorial_0to9_1_overflow),
    .ANSWER(factorial_0to9_1_answer));
  MUL_16_Bit mul_16_bit_1 (
    .B15(B15), .B14(B14), .B13(B13), .B12(B12), .B11(B11), .B10(B10), .B9(B9), .B8(B8), .B7(B7), .B6(B6),
    .B5(B5), .B4(B4), .B3(B3), .B2(B2), .B1(B1), .B0(B0), .A15(A15), .A14(A14), .A13(A13), .A12(A12),
    .A11(A11), .A10(A10), .A9(A9), .A8(A8), .A7(A7), .A6(A6), .A5(A5), .A4(A4), .A3(A3), .A2(A2), .A1(A1),
    .A0(A0), .P31(mul_16_bit_1_p0[31]), .P30(mul_16_bit_1_p0[30]), .P29(mul_16_bit_1_p0[29]),
    .P28(mul_16_bit_1_p0[28]), .P27(mul_16_bit_1_p0[27]), .P26(mul_16_bit_1_p0[26]),
    .P25(mul_16_bit_1_p0[25]), .P24(mul_16_bit_1_p0[24]), .P23(mul_16_bit_1_p0[23]),
    .P22(mul_16_bit_1_p0[22]), .P21(mul_16_bit_1_p0[21]), .P20(mul_16_bit_1_p0[20]),
    .P19(mul_16_bit_1_p0[19]), .P18(mul_16_bit_1_p0[18]), .P17(mul_16_bit_1_p0[17]),
    .P16(mul_16_bit_1_p0[16]), .P15(mul_16_bit_1_p0[15]), .P14(mul_16_bit_1_p0[14]),
    .P13(mul_16_bit_1_p0[13]), .P12(mul_16_bit_1_p0[12]), .P11(mul_16_bit_1_p0[11]),
    .P10(mul_16_bit_1_p0[10]), .P9(mul_16_bit_1_p0[9]), .P8(mul_16_bit_1_p0[8]), .P7(mul_16_bit_1_p0[7]),
    .P6(mul_16_bit_1_p0[6]), .P5(mul_16_bit_1_p0[5]), .P4(mul_16_bit_1_p0[4]), .P3(mul_16_bit_1_p0[3]),
    .P2(mul_16_bit_1_p0[2]), .P1(mul_16_bit_1_p0[1]), .P0(mul_16_bit_1_p0[0]));
  GREY_TO_BIN_16BIT grey_to_bin_16bit_1 (
    .G0(multiplexer_1_out[0]), .G1(multiplexer_1_out[1]), .G2(multiplexer_1_out[2]),
    .G3(multiplexer_1_out[3]), .G4(multiplexer_1_out[4]), .G5(multiplexer_1_out[5]),
    .G6(multiplexer_1_out[6]), .G7(multiplexer_1_out[7]), .G8(multiplexer_1_out[8]),
    .G9(multiplexer_1_out[9]), .G10(multiplexer_1_out[10]), .G11(multiplexer_1_out[11]),
    .G12(multiplexer_1_out[12]), .G13(multiplexer_1_out[13]), .G14(multiplexer_1_out[14]),
    .G15(multiplexer_1_out[15]), .B0(grey_to_bin_16bit_1_b0[0]), .B1(grey_to_bin_16bit_1_b0[1]),
    .B2(grey_to_bin_16bit_1_b0[2]), .B3(grey_to_bin_16bit_1_b0[3]), .B4(grey_to_bin_16bit_1_b0[4]),
    .B5(grey_to_bin_16bit_1_b0[5]), .B6(grey_to_bin_16bit_1_b0[6]), .B7(grey_to_bin_16bit_1_b0[7]),
    .B8(grey_to_bin_16bit_1_b0[8]), .B9(grey_to_bin_16bit_1_b0[9]), .B10(grey_to_bin_16bit_1_b0[10]),
    .B11(grey_to_bin_16bit_1_b0[11]), .B12(grey_to_bin_16bit_1_b0[12]), .B13(grey_to_bin_16bit_1_b0[13]),
    .B14(grey_to_bin_16bit_1_b0[14]), .B15(grey_to_bin_16bit_1_b0[15]));
  Power_16bit power_16bit_1 (
    .RESET(RESETT), .CLK(clock_2_out), .P15(multiplexer_2_out[15]), .P14(multiplexer_2_out[14]),
    .P13(multiplexer_2_out[13]), .P12(multiplexer_2_out[12]), .P11(multiplexer_2_out[11]),
    .P10(multiplexer_2_out[10]), .P9(multiplexer_2_out[9]), .P8(multiplexer_2_out[8]),
    .P7(multiplexer_2_out[7]), .P6(multiplexer_2_out[6]), .P5(multiplexer_2_out[5]),
    .P4(multiplexer_2_out[4]), .P3(multiplexer_2_out[3]), .P2(multiplexer_2_out[2]),
    .P1(multiplexer_2_out[1]), .P0(multiplexer_2_out[0]), .Power7(multiplexer_3_out[7]),
    .Power6(multiplexer_3_out[6]), .Power5(multiplexer_3_out[5]), .Power4(multiplexer_3_out[4]),
    .Power3(multiplexer_3_out[3]), .Power2(multiplexer_3_out[2]), .Power1(multiplexer_3_out[1]),
    .Power0(multiplexer_3_out[0]), .OUTPUTTT(power_16bit_1_outputtt));
  Log2 log2_1 (
    .A0(multiplexer_1_out[0]), .A1(multiplexer_1_out[1]), .A2(multiplexer_1_out[2]),
    .A3(multiplexer_1_out[3]), .A4(multiplexer_1_out[4]), .A5(multiplexer_1_out[5]),
    .A6(multiplexer_1_out[6]), .A7(multiplexer_1_out[7]), .A8(multiplexer_1_out[8]),
    .A9(multiplexer_1_out[9]), .A10(multiplexer_1_out[10]), .A11(multiplexer_1_out[11]),
    .A12(multiplexer_1_out[12]), .A13(multiplexer_1_out[13]), .A14(multiplexer_1_out[14]),
    .A15(multiplexer_1_out[15]), .Undefined_Value(log2_1_undefined_value), .B0(log2_1_b0[0]),
    .B1(log2_1_b0[1]), .B2(log2_1_b0[2]), .B3(log2_1_b0[3]));
  Divisor_16bit divisor_16bit_1 (
    .divisor7(multiplexer_4_out[7]), .divisor6(multiplexer_4_out[6]), .divisor5(multiplexer_4_out[5]),
    .divisor4(multiplexer_4_out[4]), .divisor3(multiplexer_4_out[3]), .divisor2(multiplexer_4_out[2]),
    .divisor1(multiplexer_4_out[1]), .divisor0(multiplexer_4_out[0]), .D15(multiplexer_5_out[15]),
    .D14(multiplexer_5_out[14]), .D13(multiplexer_5_out[13]), .D12(multiplexer_5_out[12]),
    .D11(multiplexer_5_out[11]), .D10(multiplexer_5_out[10]), .D9(multiplexer_5_out[9]),
    .D8(multiplexer_5_out[8]), .D7(multiplexer_5_out[7]), .D6(multiplexer_5_out[6]),
    .D5(multiplexer_5_out[5]), .D4(multiplexer_5_out[4]), .D3(multiplexer_5_out[3]),
    .D2(multiplexer_5_out[2]), .D1(multiplexer_5_out[1]), .D0(multiplexer_5_out[0]),
    .UNDEFINED(divisor_16bit_1_undefined), .Q15(divisor_16bit_1_q0[15]), .Q14(divisor_16bit_1_q0[14]),
    .Q13(divisor_16bit_1_q0[13]), .Q12(divisor_16bit_1_q0[12]), .Q11(divisor_16bit_1_q0[11]),
    .Q10(divisor_16bit_1_q0[10]), .Q9(divisor_16bit_1_q0[9]), .Q8(divisor_16bit_1_q0[8]),
    .Q7(divisor_16bit_1_q0[7]), .Q6(divisor_16bit_1_q0[6]), .Q5(divisor_16bit_1_q0[5]),
    .Q4(divisor_16bit_1_q0[4]), .Q3(divisor_16bit_1_q0[3]), .Q2(divisor_16bit_1_q0[2]),
    .Q1(divisor_16bit_1_q0[1]), .Q0(divisor_16bit_1_q0[0]), .R7(divisor_16bit_1_r7[24]),
    .R4(divisor_16bit_1_r7[27]), .R3(divisor_16bit_1_r7[28]), .R2(divisor_16bit_1_r7[29]),
    .R1(divisor_16bit_1_r7[30]), .R0(divisor_16bit_1_r7[31]), .R6(divisor_16bit_1_r7[25]),
    .R5(divisor_16bit_1_r7[26]));
  AND_16BIT and_16bit_1 (
    .A0(A0), .A1(A1), .A2(A2), .A3(A3), .A4(A4), .A5(A5), .A6(A6), .A7(A7), .A8(A8), .A9(A9), .A10(A10),
    .A11(A11), .A12(A12), .A13(A13), .A14(A14), .A15(A15), .B0(B0), .B1(B1), .B2(B2), .B3(B3), .B4(B4),
    .B5(B5), .B6(B6), .B7(B7), .B8(B8), .B9(B9), .B10(B10), .B11(B11), .B12(B12), .B13(B13), .B14(B14),
    .B15(B15), .X0(and_16bit_1_x0[0]), .X1(and_16bit_1_x0[1]), .X2(and_16bit_1_x0[2]),
    .X3(and_16bit_1_x0[3]), .X4(and_16bit_1_x0[4]), .X5(and_16bit_1_x0[5]), .X6(and_16bit_1_x0[6]),
    .X7(and_16bit_1_x0[7]), .X8(and_16bit_1_x0[8]), .X9(and_16bit_1_x0[9]), .X10(and_16bit_1_x0[10]),
    .X11(and_16bit_1_x0[11]), .X12(and_16bit_1_x0[12]), .X13(and_16bit_1_x0[13]), .X14(and_16bit_1_x0[14]),
    .X15(and_16bit_1_x0[15]));
  XOR_16BIT xor_16bit_1 (
    .A0(A0), .A1(A1), .A2(A2), .A3(A3), .A4(A4), .A5(A5), .A6(A6), .A7(A7), .A8(A8), .A9(A9), .A10(A10),
    .A11(A11), .A12(A12), .A13(A13), .A14(A14), .A15(A15), .B0(B0), .B1(B1), .B2(B2), .B3(B3), .B4(B4),
    .B5(B5), .B6(B6), .B7(B7), .B8(B8), .B9(B9), .B10(B10), .B11(B11), .B12(B12), .B13(B13), .B14(B14),
    .B15(B15), .X0(xor_16bit_1_x0[0]), .X1(xor_16bit_1_x0[1]), .X2(xor_16bit_1_x0[2]),
    .X3(xor_16bit_1_x0[3]), .X4(xor_16bit_1_x0[4]), .X5(xor_16bit_1_x0[5]), .X6(xor_16bit_1_x0[6]),
    .X7(xor_16bit_1_x0[7]), .X8(xor_16bit_1_x0[8]), .X9(xor_16bit_1_x0[9]), .X10(xor_16bit_1_x0[10]),
    .X11(xor_16bit_1_x0[11]), .X12(xor_16bit_1_x0[12]), .X13(xor_16bit_1_x0[13]), .X14(xor_16bit_1_x0[14]),
    .X15(xor_16bit_1_x0[15]));
  XNOR_16BIT xnor_16bit_1 (
    .A0(A0), .A1(A1), .A2(A2), .A3(A3), .A4(A4), .A5(A5), .A6(A6), .A7(A7), .A8(A8), .A9(A9), .A10(A10),
    .A11(A11), .A12(A12), .A13(A13), .A14(A14), .A15(A15), .B0(B0), .B1(B1), .B2(B2), .B3(B3), .B4(B4),
    .B5(B5), .B6(B6), .B7(B7), .B8(B8), .B9(B9), .B10(B10), .B11(B11), .B12(B12), .B13(B13), .B14(B14),
    .B15(B15), .X0(xnor_16bit_1_x0[0]), .X1(xnor_16bit_1_x0[1]), .X2(xnor_16bit_1_x0[2]),
    .X3(xnor_16bit_1_x0[3]), .X4(xnor_16bit_1_x0[4]), .X5(xnor_16bit_1_x0[5]), .X6(xnor_16bit_1_x0[6]),
    .X7(xnor_16bit_1_x0[7]), .X8(xnor_16bit_1_x0[8]), .X9(xnor_16bit_1_x0[9]), .X10(xnor_16bit_1_x0[10]),
    .X11(xnor_16bit_1_x0[11]), .X12(xnor_16bit_1_x0[12]), .X13(xnor_16bit_1_x0[13]),
    .X14(xnor_16bit_1_x0[14]), .X15(xnor_16bit_1_x0[15]));
  Subractor_16_Bit subractor_16_bit_1 (
    .A0(A0), .B0(B0), .A1(A1), .B1(B1), .A2(A2), .B2(B2), .A3(A3), .B3(B3), .A4(A4), .B4(B4), .A5(A5),
    .B5(B5), .A6(A6), .B6(B6), .A7(A7), .B7(B7), .A8(A8), .B8(B8), .A9(A9), .B9(B9), .A10(A10), .B10(B10),
    .A11(A11), .B11(B11), .A12(A12), .B12(B12), .A13(A13), .B13(B13), .A14(A14), .B14(B14), .A15(A15),
    .B15(B15), .S0(subractor_16_bit_1_s0[0]), .S1(subractor_16_bit_1_s0[1]), .S2(subractor_16_bit_1_s0[2]),
    .S3(subractor_16_bit_1_s0[3]), .S4(subractor_16_bit_1_s0[4]), .S5(subractor_16_bit_1_s0[5]),
    .S6(subractor_16_bit_1_s0[6]), .S7(subractor_16_bit_1_s0[7]), .S8(subractor_16_bit_1_s0[8]),
    .S9(subractor_16_bit_1_s0[9]), .S10(subractor_16_bit_1_s0[10]), .S11(subractor_16_bit_1_s0[11]),
    .S12(subractor_16_bit_1_s0[12]), .S13(subractor_16_bit_1_s0[13]), .S14(subractor_16_bit_1_s0[14]),
    .S15(subractor_16_bit_1_s0[15]));
  Adder_16_Bit adder_16_bit_1 (
    .A0(A0), .B0(B0), .A1(A1), .B1(B1), .A2(A2), .B2(B2), .A3(A3), .B3(B3), .A4(A4), .B4(B4), .A5(A5),
    .B5(B5), .A6(A6), .B6(B6), .A7(A7), .B7(B7), .A8(A8), .B8(B8), .A9(A9), .B9(B9), .A10(A10), .B10(B10),
    .A11(A11), .B11(B11), .A12(A12), .B12(B12), .A13(A13), .B13(B13), .A14(A14), .B14(B14), .A15(A15),
    .B15(B15), .S0(adder_16_bit_1_s0[0]), .S1(adder_16_bit_1_s0[1]), .S2(adder_16_bit_1_s0[2]),
    .S3(adder_16_bit_1_s0[3]), .S4(adder_16_bit_1_s0[4]), .S5(adder_16_bit_1_s0[5]),
    .S6(adder_16_bit_1_s0[6]), .S7(adder_16_bit_1_s0[7]), .S8(adder_16_bit_1_s0[8]),
    .S9(adder_16_bit_1_s0[9]), .S10(adder_16_bit_1_s0[10]), .S11(adder_16_bit_1_s0[11]),
    .S12(adder_16_bit_1_s0[12]), .S13(adder_16_bit_1_s0[13]), .S14(adder_16_bit_1_s0[14]),
    .S15(adder_16_bit_1_s0[15]), .S16(adder_16_bit_1_s0[16]));
  OR_16BIT or_16bit_1 (
    .A0(A0), .A1(A1), .A2(A2), .A3(A3), .A4(A4), .A5(A5), .A6(A6), .A7(A7), .A8(A8), .A9(A9), .A10(A10),
    .A11(A11), .A12(A12), .A13(A13), .A14(A14), .A15(A15), .B0(B0), .B1(B1), .B2(B2), .B3(B3), .B4(B4),
    .B5(B5), .B6(B6), .B7(B7), .B8(B8), .B9(B9), .B10(B10), .B11(B11), .B12(B12), .B13(B13), .B14(B14),
    .B15(B15), .X0(or_16bit_1_x0[0]), .X1(or_16bit_1_x0[1]), .X2(or_16bit_1_x0[2]), .X3(or_16bit_1_x0[3]),
    .X4(or_16bit_1_x0[4]), .X5(or_16bit_1_x0[5]), .X6(or_16bit_1_x0[6]), .X7(or_16bit_1_x0[7]),
    .X8(or_16bit_1_x0[8]), .X9(or_16bit_1_x0[9]), .X10(or_16bit_1_x0[10]), .X11(or_16bit_1_x0[11]),
    .X12(or_16bit_1_x0[12]), .X13(or_16bit_1_x0[13]), .X14(or_16bit_1_x0[14]), .X15(or_16bit_1_x0[15]));
  Multiplexer #(.select(4), .width(32)) multiplexer_6 (
    .in0({in_16, in_15, in_14, in_13, in_12, in_11, in_10, in_9, in_8, in_7, in_6, in_5, in_4, in_3, in_2, in_1, subractor_16_bit_1_s0}),
    .in1({{2{in_30}}, in_29, in_28, in_27, in_26, in_25, in_24, in_23, in_22, in_21, in_20, in_19, in_18, in_17, adder_16_bit_1_s0}),
    .in2({in_46, in_45, in_44, in_43, in_42, in_41, in_40, in_39, in_38, in_37, in_36, in_35, in_34, in_33, in_32, in_31, or_16bit_1_x0}),
    .in3({in_62, in_61, in_60, in_59, in_58, in_57, in_56, in_55, in_54, in_53, in_52, in_51, in_50, in_49, in_48, in_47, and_16bit_1_x0}),
    .in4({in_78, in_77, in_76, in_75, in_74, in_73, in_72, in_71, in_70, in_69, in_68, in_67, in_66, in_65, in_64, in_63, xor_16bit_1_x0}),
    .in5({in_105, in_103, in_101, in_99, in_97, in_95, in_93, in_91, in_89, in_87, in_85, in_83, in_82, in_81, in_80, in_79, xnor_16bit_1_x0}),
    .in6(mul_16_bit_1_p0),
    .in7({in_146, in_144, in_142, in_140, in_139, in_138, in_137, in_136, in_135, in_134, in_133, in_132, in_131, in_130, in_129, in_128, grey_to_bin_16bit_1_b0}),
    .in8({in_177, in_175, in_173, in_171, in_170, in_169, in_168, in_167, in_166, in_165, in_164, in_163, in_162, in_160, in_158, in_156, bitwise_left_shift_1_x0}),
    .in9({in_190, in_189, in_188, in_187, in_186, in_185, in_184, in_183, in_182, in_181, in_180, in_179, in_178, in_176, in_174, in_172, bitwise_right_shift_1_x0}),
    .in10({{28{in_191}}, log2_1_b0}),
    .in11({in_208, in_206, in_205, in_204, in_203, in_202, in_201, in_200, in_199, in_198, in_197, in_196, in_195, in_194, in_193, in_192, not_16bit_1_x0}),
    .in12({{2{in_161}}, in_159, in_157, in_155, in_154, in_153, in_152, in_151, in_150, in_149, in_148, in_147, in_145, in_143, in_141, bin_to_grey_16bit_1_g0}),
    .in13(factorial_0to9_1_answer), .in14({divisor_16bit_1_r7, {8{1'b0}}, divisor_16bit_1_q0}),
    .in15(power_16bit_1_outputtt), .out(Binary), .sel(in_207));
  LED led_1 (.in(log2_1_undefined_value[0]));
  LED LOG2_UNDEFINED (.in(log2_1_undefined_value[1]));
  Converter converter_1 (
    .Inputt(Binary), .Decimal_Quotient(Decimal_Quotient), .Binary_Quotient(Binary_Quotient),
    .Decimal_Remainder(Decimal_Remainder), .Binary_Remainder(Binay_Remainder));
  LED led_2 (.in(factorial_0to9_1_overflow[0]));
  LED FACTORIAL_OVERFLOW (.in(factorial_0to9_1_overflow[1]));
  LED led_3 (.in(divisor_16bit_1_undefined[0]));
  LED DIVISOR_UNDEFINED (.in(divisor_16bit_1_undefined[1]));

  assign Decimal = Binary;

  // Notes on the sheet:
  //   Decimal - 0
  //   Binary - 1
  //   Decimal - 0
  //   Binary - 1
  //   0000 - Subractor
  //   0001 - Adder
  //   0010 - OR
  //   0011 - AND
  //   0100 - XOR
  //   0101 - XNOR
  //   0110 - MULTIPLIER
  //   1010 - Log2
  //   1011 - NOT
  //   1101 - Factorial
  //   1110 - Divisor
  //   1111 - Power
  //   0111 - Grey To Binary
  //   1000 - Bitwise Left Shift
  //   1001 - Bitwise Right Shift
  //   1100 - Binary to Grey
endmodule
