// Logisim project Factorial_0to9.circ as structural Verilog: 1 circuit, main circuit Factorial_0to9
module Factorial_0to9 (
  input  RESET,
  input  CLK,
  input  A0,
  input  A1,
  input  A2,
  input  A3,
  output [1:0] OVERFLOW,
  output [31:0] ANSWER
);

  wire and_1_out, and_2_out, and_3_out, and_4_out, comparator_2_eq, comparator_2_gt, comparator_3_eq,
       comparator_4_gt, comparator_5_eq, comparator_5_gt, counter_1_q, or_1_out, or_2_out, or_3_out;
  wire [3:0] counter_2_q, multiplexer_2_out;
  wire [31:0] multiplexer_1_out, multiplier_16_bit_1_p0;

  Comparator #(.mode("unsigned"), .width(4)) comparator_1 (
    .a(4'b1001), .b({A3, A2, A1, A0}), .lt(OVERFLOW[1]));  // open: gt, eq
  Comparator #(.mode("unsigned"), .width(4)) comparator_2 (
    .a({A3, A2, A1, A0}), .b(counter_2_q), .gt(comparator_2_gt), .eq(comparator_2_eq));  // open: lt
  and and_1 (and_1_out, CLK, comparator_2_eq);
  and and_2 (and_2_out, CLK, comparator_2_gt);
  not not_1 (OVERFLOW[0], OVERFLOW[1]);
  or or_1 (or_1_out, and_1_out, and_2_out);
  Counter #(.max('h1), .ongoal("stay"), .width(1)) counter_1 (
    .clr(RESET), .load(1'b0), .up(1'b1), .clk(CLK), .Q(counter_1_q));  // open: count, D, carry
  Counter #(.max('hf), .ongoal("stay"), .width(4)) counter_2 (
    .clr(RESET), .load(1'b0), .up(1'b1), .clk(or_1_out), .Q(counter_2_q));  // open: count, D, carry
  Multiplexer #(.width(32)) multiplexer_1 (.in0(32'h1), .in1(ANSWER), .out(multiplexer_1_out), .sel(counter_1_q));
  Comparator #(.mode("unsigned"), .width(4)) comparator_3 (
    .a(4'b0000), .b(counter_2_q), .eq(comparator_3_eq));  // open: gt, lt
  Comparator #(.mode("unsigned"), .width(4)) comparator_4 (
    .a(counter_2_q), .b({A3, A2, A1, A0}), .gt(comparator_4_gt));  // open: eq, lt
  Multiplexer #(.width(4)) multiplexer_2 (.in0(counter_2_q), .in1(4'b0001), .out(multiplexer_2_out), .sel(or_2_out));
  or or_2 (or_2_out, comparator_3_eq, comparator_4_gt);
  Multiplier_16_Bit multiplier_16_bit_1 (
    .B15(multiplexer_1_out[15]), .B14(multiplexer_1_out[14]), .B13(multiplexer_1_out[13]),
    .B12(multiplexer_1_out[12]), .B11(multiplexer_1_out[11]), .B10(multiplexer_1_out[10]),
    .B9(multiplexer_1_out[9]), .B8(multiplexer_1_out[8]), .B7(multiplexer_1_out[7]),
    .B6(multiplexer_1_out[6]), .B5(multiplexer_1_out[5]), .B4(multiplexer_1_out[4]),
    .B3(multiplexer_1_out[3]), .B2(multiplexer_1_out[2]), .B1(multiplexer_1_out[1]),
    .B0(multiplexer_1_out[0]), .A15(1'b0), .A14(1'b0), .A13(1'b0), .A12(1'b0), .A11(1'b0), .A10(1'b0),
    .A9(1'b0), .A8(1'b0), .A7(1'b0), .A6(1'b0), .A5(1'b0), .A4(1'b0), .A3(multiplexer_2_out[3]),
    .A2(multiplexer_2_out[2]), .A1(multiplexer_2_out[1]), .A0(multiplexer_2_out[0]),
    .P31(multiplier_16_bit_1_p0[31]), .P30(multiplier_16_bit_1_p0[30]), .P29(multiplier_16_bit_1_p0[29]),
    .P28(multiplier_16_bit_1_p0[28]), .P27(multiplier_16_bit_1_p0[27]), .P26(multiplier_16_bit_1_p0[26]),
    .P25(multiplier_16_bit_1_p0[25]), .P24(multiplier_16_bit_1_p0[24]), .P23(multiplier_16_bit_1_p0[23]),
    .P22(multiplier_16_bit_1_p0[22]), .P21(multiplier_16_bit_1_p0[21]), .P20(multiplier_16_bit_1_p0[20]),
    .P19(multiplier_16_bit_1_p0[19]), .P18(multiplier_16_bit_1_p0[18]), .P17(multiplier_16_bit_1_p0[17]),
    .P16(multiplier_16_bit_1_p0[16]), .P15(multiplier_16_bit_1_p0[15]), .P14(multiplier_16_bit_1_p0[14]),
    .P13(multiplier_16_bit_1_p0[13]), .P12(multiplier_16_bit_1_p0[12]), .P11(multiplier_16_bit_1_p0[11]),
    .P10(multiplier_16_bit_1_p0[10]), .P9(multiplier_16_bit_1_p0[9]), .P8(multiplier_16_bit_1_p0[8]),
    .P7(multiplier_16_bit_1_p0[7]), .P6(multiplier_16_bit_1_p0[6]), .P5(multiplier_16_bit_1_p0[5]),
    .P4(multiplier_16_bit_1_p0[4]), .P3(multiplier_16_bit_1_p0[3]), .P2(multiplier_16_bit_1_p0[2]),
    .P1(multiplier_16_bit_1_p0[1]), .P0(multiplier_16_bit_1_p0[0]));
  Comparator #(.mode("unsigned"), .width(4)) comparator_5 (
    .a(4'b1001), .b(counter_2_q), .gt(comparator_5_gt), .eq(comparator_5_eq));  // open: lt
  and and_3 (and_3_out, CLK, comparator_5_gt);
  and and_4 (and_4_out, CLK, comparator_5_eq);
  Register #(.width(32)) register_1 (.D(multiplier_16_bit_1_p0), .clk(or_3_out), .Q(ANSWER));  // open: en, clr
  or or_3 (or_3_out, and_3_out, and_4_out);
endmodule
