// Logisim project Power_16Bit.circ as structural Verilog: 1 circuit, main circuit Power_16bit
module Power_16bit (
  input  RESET,
  input  CLK,
  input  P15,
  input  P14,
  input  P13,
  input  P12,
  input  P11,
  input  P10,
  input  P9,
  input  P8,
  input  P7,
  input  P6,
  input  P5,
  input  P4,
  input  P3,
  input  P2,
  input  P1,
  input  P0,
  input  Power7,
  input  Power6,
  input  Power5,
  input  Power4,
  input  Power3,
  input  Power2,
  input  Power1,
  input  Power0,
  output [31:0] OUTPUTTT
);

  wire and_1_out, comparator_1_lt, counter_1_q;
  wire [7:0] counter_2_q;
  wire [31:0] multiplexer_1_out, multiplier_16_bit_1_p0;

  Counter #(.max('h1), .ongoal("stay"), .width(1)) counter_1 (
    .clr(RESET), .load(1'b0), .up(1'b1), .clk(CLK), .Q(counter_1_q));  // open: count, D, carry
  Multiplexer #(.width(32)) multiplexer_1 (.in0(32'h1), .in1(OUTPUTTT), .out(multiplexer_1_out), .sel(counter_1_q));
  Multiplier_16_Bit multiplier_16_bit_1 (
    .B15(multiplexer_1_out[15]), .B14(multiplexer_1_out[14]), .B13(multiplexer_1_out[13]),
    .B12(multiplexer_1_out[12]), .B11(multiplexer_1_out[11]), .B10(multiplexer_1_out[10]),
    .B9(multiplexer_1_out[9]), .B8(multiplexer_1_out[8]), .B7(multiplexer_1_out[7]),
    .B6(multiplexer_1_out[6]), .B5(multiplexer_1_out[5]), .B4(multiplexer_1_out[4]),
    .B3(multiplexer_1_out[3]), .B2(multiplexer_1_out[2]), .B1(multiplexer_1_out[1]),
    .B0(multiplexer_1_out[0]), .A15(P15), .A14(P14), .A13(P13), .A12(P12), .A11(P11), .A10(P10), .A9(P9),
    .A8(P8), .A7(P7), .A6(P6), .A5(P5), .A4(P4), .A3(P3), .A2(P2), .A1(P1), .A0(P0),
    .P31(multiplier_16_bit_1_p0[31]), .P30(multiplier_16_bit_1_p0[30]), .P29(multiplier_16_bit_1_p0[29]),
    .P28(multiplier_16_bit_1_p0[28]), .P27(multiplier_16_bit_1_p0[27]), .P26(multiplier_16_bit_1_p0[26]),
    .P25(multiplier_16_bit_1_p0[25]), .P24(multiplier_16_bit_1_p0[24]), .P23(multiplier_16_bit_1_p0[23]),
    .P22(multiplier_16_bit_1_p0[22]), .P21(multiplier_16_bit_1_p0[21]), .P20(multiplier_16_bit_1_p0[20]),
    .P19(multiplier_16_bit_1_p0[19]), .P18(multiplier_16_bit_1_p0[18]), .P17(multiplier_16_bit_1_p0[17]),
    .P16(multiplier_16_bit_1_p0[16]), .P15(multiplier_16_bit_1_p0[15]), .P14(multiplier_16_bit_1_p0[14]),
    .P13(multiplier_16_bit_1_p0[13]), .P12(multiplier_16_bit_1_p0[12]), .P11(multiplier_16_bit_1_p0[11]),
    .P10(multiplier_16_bit_1_p0[10]), .P9(multiplier_16_bit_1_p0[9]), .P8(multiplier_16_bit_1_p0[8]),
    .P7(multiplier_16_bit_1_p0[7]), .P6(multiplier_16_bit_1_p0[6]), .P5(multiplier_16_bit_1_p0[5]),
    .P4(multiplier_16_bit_1_p0[4]), .P3(multiplier_16_bit_1_p0[3]), .P2(multiplier_16_bit_1_p0[2]),
    .P1(multiplier_16_bit_1_p0[1]), .P0(multiplier_16_bit_1_p0[0]));
  Counter #(.ongoal("stay")) counter_2 (
    .clr(RESET), .load(1'b0), .up(1'b1), .clk(CLK), .Q(counter_2_q));  // open: count, D, carry
  Comparator #(.mode("unsigned")) comparator_1 (
    .a(counter_2_q), .b({Power7, Power6, Power5, Power4, Power3, Power2, Power1, Power0}),
    .lt(comparator_1_lt));  // open: gt, eq
  and and_1 (and_1_out, CLK, comparator_1_lt);
  Register #(.width(32)) register_1 (.D(multiplier_16_bit_1_p0), .clk(and_1_out), .Q(OUTPUTTT));  // open: en, clr
endmodule
